# Fritzing sketch ESP32_Board (saved by Fritzing 0.9.6b)
breadboards: 1

parts:
  R1 = Resistor [tolerance=±5% resistance=4.7k package="1206 [SMD]"]
  J1 = JST-03JQ-BT [part_number=JST-JQ-BT package=THT]
  J2 = JST-03JQ-BT [part_number=JST-JQ-BT package=THT]
  J3 = JST-03JQ-BT [part_number=JST-JQ-BT package=THT]
  J4 = JST-03JQ-BT [part_number=JST-JQ-BT package=THT]
  J5 = JST-03JQ-BT [part_number=JST-JQ-BT package=THT]
  J6 = JST-03JQ-BT [part_number=JST-JQ-BT package=THT]
  U1 = JST XH 4A 2.54mm [package=THT]
  U2 = JST XH 4A 2.54mm [package=THT]
  U3 = JST XH 4A 2.54mm [package=THT]
  J7 = female pin header, 21 pins [form="♀ (female)"]
  J8 = female pin header, 21 pins [form="♀ (female)"]
  M1 = ESP32-S2-DevKitM-1 [part_number=ESP32-S2-DevKitM-1]

nets:
  N1: R1.Pin_0, J1.pin1, J2.pin1, J3.pin1, J4.pin1, J5.pin1, J6.pin1, U1.pin1, U2.pin1, U3.pin1, J7.pin21, M1.3V3
  N2: R1.Pin_1, J1.pin2, J2.pin2, J3.pin2, J4.pin2, J5.pin2, J7.pin12, M1.8
  N3: J1.pin3, J2.pin3, J3.pin3, J4.pin3, J5.pin3, J6.pin3, U1.pin4, U2.pin4, U3.pin4, J7.pin1, J8.pin21, M1.G-21, M1.G-42
  N4: J6.pin2, J7.pin6, M1.14
  N5: U1.pin2, U2.pin2, U3.pin2, J8.pin13, M1.40
  N6: U1.pin3, U2.pin3, U3.pin3, J8.pin12, M1.39
  N7: J7.pin2, M1.5V
  N8: J7.pin3, M1.17
  N9: J7.pin4, M1.16
  N10: J7.pin5, M1.15
  N11: J7.pin7, M1.13
  N12: J7.pin8, M1.12
  N13: J7.pin9, M1.11
  N14: J7.pin10, M1.10
  N15: J7.pin11, M1.9
  N16: J7.pin13, M1.7
  N17: J7.pin14, M1.6
  N18: J7.pin15, M1.5
  N19: J7.pin16, M1.4
  N20: J7.pin17, M1.3
  N21: J7.pin18, M1.2
  N22: J7.pin19, M1.1
  N23: J7.pin20, M1.0
  N24: J8.pin1, M1.18
  N25: J8.pin2, M1.19
  N26: J8.pin3, M1.20
  N27: J8.pin4, M1.21
  N28: J8.pin5, M1.26
  N29: J8.pin6, M1.33
  N30: J8.pin7, M1.34
  N31: J8.pin8, M1.35
  N32: J8.pin9, M1.36
  N33: J8.pin10, M1.37
  N34: J8.pin11, M1.38
  N35: J8.pin14, M1.41
  N36: J8.pin15, M1.42
  N37: J8.pin16, M1.TX
  N38: J8.pin17, M1.RX
  N39: J8.pin18, M1.45
  N40: J8.pin19, M1.46
  N41: J8.pin20, M1.RST

notes:
  Ds18
  SHT
  OLED
  UVB

custom parts:
  JST XH 4A 2.54mm: 4 Pin JST XH connector
  ESP32-S2-DevKitM-1: The DOIT Esp32 DevKit v1 is one of the development board created by DOIT to evaluate the ESP-WROOM-32 module. It is based on the ESP32 microcontroller that boasts Wifi, Bluetooth, Ethernet and Low Power support all in a single chip. (vanepp) Feb 2021: converted to ESP32-S2-DevKitM-1. This module is 42pins long (2x21) and 11 pins width.
